# Fritzing sketch ledbrink-rpi2 (saved by Fritzing 0.9.3b)
breadboards: 1

parts:
  Raspberry_Pi_B_rev1 = Raspberry Pi B rev1
  R1 = Resistor [tolerance=±5% resistance=220 package=THT]
  LED1 = LED - 5mm [color="Red (633nm)" package="5 mm [THT]"]

nets:
  N1: Raspberry_Pi_B_rev1.GND, R1.Pin_0
  N2: Raspberry_Pi_B_rev1.GPIO_7, R1.Pin_1, LED1.cathode, LED1.anode
